# Fritzing sketch Diagrama computadora de vuelo (saved by Fritzing 0.9.3b)
breadboards: 1

parts:
  Componente2 = Arduino Nano (Rev3.0)
  GY1 = MPU-6050 Board GY-521 [form="♀ (female)" package=THT]
  U1 = GY BM E/P 280 [package="SIP (Single Inline) [THT]"]
  SD_card_module1 = SD Card Module

nets:
  GND: Componente2.GND, GY1.pin2, GY1.pin7, U1.GND, SD_card_module1.GND#0
  N1: Componente2.D2, GY1.pin8
  N2: Componente2.D10, SD_card_module1.CS
  N3: Componente2.D11/MOSI, SD_card_module1.MOSI
  N4: Componente2.D12/MISO, SD_card_module1.MISO
  5V: Componente2.5V, GY1.pin1, U1.VCC, SD_card_module1.+5
  N5: Componente2.A5, GY1.pin3, U1.SCK
  N6: Componente2.A4, GY1.pin4, U1.SDI
  N7: Componente2.D13/SCK, SD_card_module1.SCK

custom parts:
  MPU-6050 Board GY-521: Acelerometro y Giroscopio MPU-6050 Board GY-521
  GY BM E/P 280: A SIP stand-in part for whatever you want. With 6 pins on a 300 mil single inline package (SIP) footprint.
  SD Card Module: SD Card Module Slot Socket Reader For Arduino ARM MCU
